# Fritzing sketch alt-button-matrix (saved by Fritzing 0.8.0b)
breadboards: 1

parts:
  D1 = Rectifier Diode [part_number=1N4001 package="300 mil [THT]"]
  J3 = rounded female pin header, 1 pin [form="♀ (female rounded)"]
  D2 = Rectifier Diode [part_number=1N4001 package="300 mil [THT]"]
  WS2812b1 = WS2812b RGB LED
  S2 = Pushbutton [package="[SMD]"]
  S1 = Pushbutton [package="[SMD]"]
  WS2812b2 = WS2812b RGB LED
  J5 = rounded female pin header, 1 pin [form="♀ (female rounded)"]
  D3 = Rectifier Diode [part_number=1N4001 package="300 mil [THT]"]
  WS2812b3 = WS2812b RGB LED
  S3 = Pushbutton [package="[SMD]"]
  J9 = rounded female pin header, 1 pin [form="♀ (female rounded)"]
  J10 = rounded female pin header, 1 pin [form="♀ (female rounded)"]
  D4 = Rectifier Diode [part_number=1N4001 package="300 mil [THT]"]
  S4 = Pushbutton [package="[SMD]"]
  WS2812b4 = WS2812b RGB LED
  J13 = rounded female pin header, 1 pin [form="♀ (female rounded)"]
  J6 = single row smd rounded female pin header, 1 pin [form="♀ (female rounded)"]
  J7 = single row smd rounded female pin header, 1 pin [form="♀ (female rounded)"]
  J12 = single row smd rounded female pin header, 1 pin [form="♀ (female rounded)"]
  J11 = single row smd rounded female pin header, 1 pin [form="♀ (female rounded)"]
  J15 = single row smd rounded female pin header, 1 pin [form="♀ (female rounded)"]
  J2 = single row smd rounded female pin header, 1 pin [form="♀ (female rounded)"]
  J4 = single row smd rounded female pin header, 1 pin [form="♀ (female rounded)"]
  J8 = single row smd rounded female pin header, 1 pin [form="♀ (female rounded)"]
  C1 = Ceramic Capacitor [capacitance=100nF package="100 mil [THT, multilayer]"]
  C2 = Ceramic Capacitor [capacitance=100nF package="100 mil [THT, multilayer]"]
  C3 = Ceramic Capacitor [capacitance=100nF package="100 mil [THT, multilayer]"]
  C4 = Ceramic Capacitor [capacitance=100nF package="100 mil [THT, multilayer]"]
  J14 = rounded female pin header, 1 pin [form="♀ (female rounded)"]
  J17 = rounded female pin header, 1 pin [form="♀ (female rounded)"]
  J16 = rounded female pin header, 1 pin [form="♀ (female rounded)"]
  BUTTON4 = Pressure sensor
  J18 = rounded female pin header, 1 pin [form="♀ (female rounded)"]
  J19 = rounded female pin header, 1 pin [form="♀ (female rounded)"]
  BUTTON5 = Pressure sensor
  J20 = rounded female pin header, 1 pin [form="♀ (female rounded)"]
  J21 = rounded female pin header, 1 pin [form="♀ (female rounded)"]
  BUTTON6 = Pressure sensor
  J22 = rounded female pin header, 1 pin [form="♀ (female rounded)"]
  J23 = rounded female pin header, 1 pin [form="♀ (female rounded)"]
  BUTTON7 = Pressure sensor

nets:
  N1: D1.cathode, S1.Pin_2
  N2: D1.anode, D3.anode, J15.pin1, J2.pin1
  N3: J3.pin1, S2.Pin_3, S2.Pin_4, S1.Pin_3, S1.Pin_4, J7.pin1
  N4: D2.cathode, S2.Pin_2
  N5: D2.anode, D4.anode, J4.pin1, J8.pin1
  VCC: WS2812b1.vcc, WS2812b2.vcc, WS2812b3.vcc, WS2812b4.vcc, C1.0, C2.0, C3.0, C4.0, J14.pin1
  GND: WS2812b1.gnd, WS2812b2.gnd, WS2812b3.gnd, WS2812b4.gnd, J13.pin1, C1.1, C2.1, C3.1, C4.1
  N6: WS2812b1.din, J5.pin1
  N7: WS2812b1.dout, WS2812b2.din
  N8: WS2812b2.dout, J6.pin1
  N9: D3.cathode, S3.Pin_2
  N10: WS2812b3.din, J9.pin1
  N11: WS2812b3.dout, WS2812b4.din
  N12: S3.Pin_3, S3.Pin_4, J10.pin1, S4.Pin_3, S4.Pin_4, J11.pin1
  N13: D4.cathode, S4.Pin_2
  N14: WS2812b4.dout, J12.pin1
  N15: J17.pin1, BUTTON4.pin1
  N16: J16.pin1, BUTTON4.pin2
  N17: J18.pin1, BUTTON5.pin1
  N18: J19.pin1, BUTTON5.pin2
  N19: J20.pin1, BUTTON6.pin2
  N20: J21.pin1, BUTTON6.pin1
  N21: J22.pin1, BUTTON7.pin2
  N22: J23.pin1, BUTTON7.pin1

custom parts:
  WS2812b RGB LED: RGB LED
