# Fritzing sketch midi-controller-teensy (saved by Fritzing 0.8.0b)
breadboards: 1

parts:
  Teensy_3_1 = Teensy 3.0 [part_number=Controller]
  J2 = longpad pin header, 8 pins [form="long pad"]
  J3 = longpad pin header, 8 pins [form="long pad" part_number="column feed"]
  J4 = longpad pin header, 8 pins [form="long pad" part_number="LCD display"]
  R1 = Resistor [tolerance=±5% resistance=220 package="1206 [SMD]"]
  R2 = Resistor [tolerance=±5% resistance=220 package="1206 [SMD]"]
  R3 = Resistor [tolerance=±5% resistance=220 package="1206 [SMD]"]
  R4 = Resistor [tolerance=±5% resistance=220 package="1206 [SMD]"]
  R6 = Resistor [tolerance=±5% resistance=220 package="1206 [SMD]"]
  R7 = Resistor [tolerance=±5% resistance=220 package="1206 [SMD]"]
  R8 = Resistor [tolerance=±5% resistance=220 package="1206 [SMD]"]
  R5 = Resistor [tolerance=±5% resistance=220 package="1206 [SMD]"]

nets:
  N1: Teensy_3_1.GND, J4.pin7, J4.pin8
  N2: Teensy_3_1.D0, J3.pin1
  N3: Teensy_3_1.D1, J3.pin2
  N4: Teensy_3_1.D2, J3.pin3
  N5: Teensy_3_1.D3, J3.pin4
  N6: Teensy_3_1.D4, J3.pin5
  N7: Teensy_3_1.D5, J3.pin6
  N8: Teensy_3_1.D6, J3.pin7
  N9: Teensy_3_1.D7, J3.pin8
  N10: Teensy_3_1.D8, J4.pin1
  N11: Teensy_3_1.D9, J4.pin2
  N12: Teensy_3_1.D10, J4.pin3
  N13: Teensy_3_1.D11, J4.pin4
  N14: Teensy_3_1.D12, J4.pin5
  N15: Teensy_3_1.3V3, J4.pin6
  N16: Teensy_3_1.A0/D14, J2.pin1, R8.Pin_0
  N17: Teensy_3_1.A1/D15, J2.pin2, R7.Pin_0
  N18: Teensy_3_1.A2/D16, J2.pin3, R6.Pin_0
  N19: Teensy_3_1.A3/D17, J2.pin4, R5.Pin_0
  N20: Teensy_3_1.A4/D18, J2.pin5, R4.Pin_0
  N21: Teensy_3_1.A5/D19, J2.pin6, R3.Pin_0
  N22: Teensy_3_1.A6/D20, J2.pin7, R2.Pin_0
  N23: Teensy_3_1.A7/D21, J2.pin8, R1.Pin_0
  N24: Teensy_3_1.AGND, R1.Pin_1, R2.Pin_1, R3.Pin_1, R4.Pin_1, R6.Pin_1, R7.Pin_1, R8.Pin_1, R5.Pin_1

notes:
  Analog in
  1
  Column feed
  LCD display
