# Fritzing sketch pressure-button-4x4-double (saved by Fritzing 0.8.0b)
breadboards: 1

parts:
  C1 = Ceramic Capacitor [capacitance=100nF package="100 mil [THT, multilayer]"]
  C2 = Ceramic Capacitor [capacitance=100nF package="100 mil [THT, multilayer]"]
  J6 = female pin header, 1 pin [form="♀ (female)"]
  J2 = female pin header, 1 pin [form="♀ (female)"]
  C3 = Ceramic Capacitor [capacitance=100nF package="100 mil [THT, multilayer]"]
  C4 = Ceramic Capacitor [capacitance=100nF package="100 mil [THT, multilayer]"]
  J9 = female pin header, 1 pin [form="♀ (female)"]
  C5 = Ceramic Capacitor [capacitance=100nF package="100 mil [THT, multilayer]"]
  C6 = Ceramic Capacitor [capacitance=100nF package="100 mil [THT, multilayer]"]
  J15 = female pin header, 1 pin [form="♀ (female)"]
  J17 = female pin header, 1 pin [form="♀ (female)"]
  J18 = female pin header, 1 pin [form="♀ (female)"]
  C14 = Ceramic Capacitor [capacitance=100nF package="100 mil [THT, multilayer]"]
  C15 = Ceramic Capacitor [capacitance=100nF package="100 mil [THT, multilayer]"]
  C16 = Ceramic Capacitor [capacitance=100nF package="100 mil [THT, multilayer]"]
  C17 = Ceramic Capacitor [capacitance=100nF package="100 mil [THT, multilayer]"]
  C18 = Ceramic Capacitor [capacitance=100nF package="100 mil [THT, multilayer]"]
  C19 = Ceramic Capacitor [capacitance=100nF package="100 mil [THT, multilayer]"]
  C20 = Ceramic Capacitor [capacitance=100nF package="100 mil [THT, multilayer]"]
  C21 = Ceramic Capacitor [capacitance=100nF package="100 mil [THT, multilayer]"]
  C22 = Ceramic Capacitor [capacitance=100nF package="100 mil [THT, multilayer]"]
  J4 = female pin header, 1 pin [form="♀ (female)"]
  J7 = female pin header, 1 pin [form="♀ (female)"]
  J10 = female pin header, 1 pin [form="♀ (female)"]
  BUTTON27 = Pressure button WS2812b
  BUTTON16 = Pressure button WS2812b
  BUTTON23 = Pressure button WS2812b
  BUTTON14 = Pressure button WS2812b
  BUTTON26 = Pressure button WS2812b
  BUTTON28 = Pressure button WS2812b
  BUTTON22 = Pressure button WS2812b
  BUTTON21 = Pressure button WS2812b
  BUTTON20 = Pressure button WS2812b
  BUTTON17 = Pressure button WS2812b
  BUTTON19 = Pressure button WS2812b
  BUTTON13 = Pressure button WS2812b
  BUTTON15 = Pressure button WS2812b
  BUTTON24 = Pressure button WS2812b
  BUTTON18 = Pressure button WS2812b
  BUTTON25 = Pressure button WS2812b
  J20 = female pin header, 1 pin [form="♀ (female)"]
  J21 = female pin header, 1 pin [form="♀ (female)"]
  J22 = female pin header, 1 pin [form="♀ (female)"]
  D14 = Rectifier Diode [part_number=1N4001 package="300 mil [THT]"]
  C13 = Ceramic Capacitor [capacitance=100nF package="100 mil [THT, multilayer]"]
  D15 = Rectifier Diode [part_number=1N4001 package="300 mil [THT]"]
  D16 = Rectifier Diode [part_number=1N4001 package="300 mil [THT]"]
  D10 = Rectifier Diode [part_number=1N4001 package="300 mil [THT]"]
  D9 = Rectifier Diode [part_number=1N4001 package="300 mil [THT]"]
  D8 = Rectifier Diode [part_number=1N4001 package="300 mil [THT]"]
  D17 = Rectifier Diode [part_number=1N4001 package="300 mil [THT]"]
  D13 = Rectifier Diode [part_number=1N4001 package="300 mil [THT]"]
  D12 = Rectifier Diode [part_number=1N4001 package="300 mil [THT]"]
  D11 = Rectifier Diode [part_number=1N4001 package="300 mil [THT]"]
  D5 = Rectifier Diode [part_number=1N4001 package="300 mil [THT]"]
  D6 = Rectifier Diode [part_number=1N4001 package="300 mil [THT]"]
  D2 = Rectifier Diode [part_number=1N4001 package="300 mil [THT]"]
  D3 = Rectifier Diode [part_number=1N4001 package="300 mil [THT]"]
  D4 = Rectifier Diode [part_number=1N4001 package="300 mil [THT]"]
  D7 = Rectifier Diode [part_number=1N4001 package="300 mil [THT]"]
  J23 = single row smd female pin header, 1 pin [form="♀ (female)"]
  J8 = single row smd female pin header, 1 pin [form="♀ (female)"]
  J11 = single row smd female pin header, 1 pin [form="♀ (female)"]
  J5 = single row smd female pin header, 1 pin [form="♀ (female)"]
  J12 = single row smd female pin header, 1 pin [form="♀ (female)"]
  J13 = single row smd female pin header, 1 pin [form="♀ (female)"]
  J14 = single row smd female pin header, 1 pin [form="♀ (female)"]
  J19 = single row smd female pin header, 1 pin [form="♀ (female)"]
  J24 = single row smd female pin header, 1 pin [form="♀ (female)"]
  J25 = single row smd female pin header, 1 pin [form="♀ (female)"]
  J26 = single row smd female pin header, 1 pin [form="♀ (female)"]
  J27 = single row smd female pin header, 1 pin [form="♀ (female)"]
  J28 = female pin header, 1 pin [form="♀ (female)"]
  J29 = female pin header, 1 pin [form="♀ (female)"]
  J30 = female pin header, 1 pin [form="♀ (female)"]
  J31 = female pin header, 1 pin [form="♀ (female)"]

nets:
  GND: C1.0, C2.0, C3.0, C4.0, C5.0, C6.0, C14.0, C15.0, C16.0, C17.0, C18.0, C19.0, C20.0, C21.0, C22.0, BUTTON27.gnd, BUTTON16.gnd, BUTTON23.gnd, BUTTON14.gnd, BUTTON26.gnd, BUTTON28.gnd, BUTTON22.gnd, BUTTON21.gnd, BUTTON20.gnd, BUTTON17.gnd, BUTTON19.gnd, BUTTON13.gnd, BUTTON15.gnd, BUTTON24.gnd, BUTTON18.gnd, BUTTON25.gnd, C13.0, J12.pin1, J27.pin1
  VCC: C1.1, C2.1, C3.1, C4.1, C5.1, C6.1, C14.1, C15.1, C16.1, C17.1, C18.1, C19.1, C20.1, C21.1, C22.1, BUTTON27.vcc, BUTTON16.vcc, BUTTON23.vcc, BUTTON14.vcc, BUTTON26.vcc, BUTTON28.vcc, BUTTON22.vcc, BUTTON21.vcc, BUTTON20.vcc, BUTTON17.vcc, BUTTON19.vcc, BUTTON13.vcc, BUTTON15.vcc, BUTTON24.vcc, BUTTON18.vcc, BUTTON25.vcc, C13.1, J11.pin1, J19.pin1
  N1: J6.pin1, BUTTON16.ba2, BUTTON16.bb2, BUTTON28.ba2, BUTTON28.bb2, BUTTON17.ba2, BUTTON17.bb2, BUTTON24.ba2, BUTTON24.bb2, J28.pin1
  N2: J2.pin1, BUTTON27.ba2, BUTTON27.bb2, BUTTON23.ba2, BUTTON23.bb2, BUTTON15.ba2, BUTTON15.bb2, BUTTON18.ba2, BUTTON18.bb2, J29.pin1
  N3: J9.pin1, BUTTON21.ba2, BUTTON21.bb2, BUTTON20.ba2, BUTTON20.bb2, BUTTON13.ba2, BUTTON13.bb2, BUTTON25.ba2, BUTTON25.bb2, J31.pin1
  N4: J15.pin1, BUTTON25.dout
  N5: J17.pin1, BUTTON14.ba2, BUTTON14.bb2, BUTTON26.ba2, BUTTON26.bb2, BUTTON22.ba2, BUTTON22.bb2, BUTTON19.ba2, BUTTON19.bb2, J30.pin1
  N6: J18.pin1, BUTTON16.din
  N7: J4.pin1, BUTTON15.din
  N8: J7.pin1, BUTTON14.din
  N9: J10.pin1, BUTTON13.din
  N10: BUTTON27.ba1, BUTTON27.bb1, D13.cathode
  N11: BUTTON27.din, BUTTON23.dout
  N12: BUTTON27.dout, J21.pin1
  N13: BUTTON16.ba1, BUTTON16.bb1, D14.cathode
  N14: BUTTON16.dout, BUTTON17.din
  N15: BUTTON23.ba1, BUTTON23.bb1, D10.cathode
  N16: BUTTON23.din, BUTTON18.dout
  N17: BUTTON14.ba1, BUTTON14.bb1, D4.cathode
  N18: BUTTON14.dout, BUTTON19.din
  N19: BUTTON26.ba1, BUTTON26.bb1, D12.cathode
  N20: BUTTON26.din, BUTTON22.dout
  N21: BUTTON26.dout, J20.pin1
  N22: BUTTON28.ba1, BUTTON28.bb1, D17.cathode
  N23: BUTTON28.din, BUTTON24.dout
  N24: BUTTON28.dout, J22.pin1
  N25: BUTTON22.ba1, BUTTON22.bb1, D9.cathode
  N26: BUTTON22.din, BUTTON19.dout
  N27: BUTTON21.ba1, BUTTON21.bb1, D8.cathode
  N28: BUTTON21.din, BUTTON20.dout
  N29: BUTTON21.dout, BUTTON25.din
  N30: BUTTON20.ba1, BUTTON20.bb1, D6.cathode
  N31: BUTTON20.din, BUTTON13.dout
  N32: BUTTON17.ba1, BUTTON17.bb1, D15.cathode
  N33: BUTTON17.dout, BUTTON24.din
  N34: BUTTON19.ba1, BUTTON19.bb1, D5.cathode
  N35: BUTTON13.ba1, BUTTON13.bb1, D7.cathode
  N36: BUTTON15.ba1, BUTTON15.bb1, D3.cathode
  N37: BUTTON15.dout, BUTTON18.din
  N38: BUTTON24.ba1, BUTTON24.bb1, D16.cathode
  N39: BUTTON18.ba1, BUTTON18.bb1, D2.cathode
  N40: BUTTON25.ba1, BUTTON25.bb1, D11.cathode
  N41: D14.anode, D3.anode, D4.anode, D7.anode, J23.pin1, J5.pin1
  N42: D15.anode, D5.anode, D6.anode, D2.anode, J8.pin1, J24.pin1
  N43: D16.anode, D10.anode, D9.anode, D8.anode, J13.pin1, J25.pin1
  N44: D17.anode, D13.anode, D12.anode, D11.anode, J14.pin1, J26.pin1

custom parts:
  Pressure button WS2812b: Pressure button with LED
